// Logisim project Digital Project 1.circ as structural Verilog: 1 circuit, main circuit main
module main (
  input  [3:0] A,
  input  [3:0] B,
  input  [2:0] AluOp,
  input  en,
  output Zero,
  output [3:0] Result
);

  wire n7404_1_p2, n7404_1_p4, n7404_1_p5, n7408_1_p3, n7408_1_p4, n7408_1_p9, n7408_1_p10, n7408_1_p17,
       n7408_1_p18, n7408_1_p19, n7408_1_p25, n7408_1_p26, n7408_1_p27, n7432_1_p3, n7432_1_p9, n7486_1_p3,
       n7486_1_p9;

  // _7408 7408_1: pin names not known; wires that end beside it: 1'b0, 1'b0, n7408_1_p3, n7408_1_p4, A[2], B[1], B[2], A[1], n7408_1_p9, n7408_1_p10, A[3], B[0], B[3], A[0], 1'b1, n7408_1_p9, n7408_1_p17, n7408_1_p18, n7408_1_p19, A[2], 1'b0, A[3], B[2], n7408_1_p3, n7408_1_p25, n7408_1_p26, n7408_1_p27
  // _7432 7432_1: pin names not known; wires that end beside it: 1'b0, n7408_1_p25, n7432_1_p3, A[2], B[1], B[2], A[1], n7408_1_p17, n7432_1_p9, A[3], B[0], B[3], A[0], 1'b1
  // _7486 7486_1: pin names not known; wires that end beside it: 1'b0, n7408_1_p26, n7486_1_p3, A[2], B[1], B[2], A[1], n7408_1_p18, n7486_1_p9, A[3], B[0], B[3], A[0], 1'b1
  // _7404 7404_1: pin names not known; wires that end beside it: 1'b0, n7404_1_p2, n7486_1_p9, n7404_1_p4, n7404_1_p5, en, n7486_1_p3, n7408_1_p19, n7408_1_p27, n7408_1_p18, n7408_1_p26, 1'b1
  // _74151 74151_1: pin names not known; wires that end beside it: 1'b1, n7408_1_p19, A[2], n7408_1_p18, 1'b0, n7408_1_p17, A[3], n7408_1_p9, B[2], Result[3], AluOp[0], AluOp[1], n7404_1_p4
  // _74151 74151_2: pin names not known; wires that end beside it: AluOp[2], 1'b0, 1'b1, n7408_1_p27, A[1], n7408_1_p26, A[3], n7408_1_p25, A[3], n7408_1_p3, B[1], Result[2], AluOp[0]
  // _7425 7425_1: pin names not known; wires that end beside it: 1'b0, Zero, Result[3], Result[2], Result[1], Result[0], 1'b1
  // _74151 74151_3: pin names not known; wires that end beside it: AluOp[1], n7404_1_p4, AluOp[2], 1'b0, 1'b1, n7404_1_p5, A[0], n7486_1_p3, A[2], n7432_1_p3, A[2], n7408_1_p4, B[0], Result[1], AluOp[0]
  // _74151 74151_4: pin names not known; wires that end beside it: AluOp[1], n7404_1_p4, AluOp[2], 1'b0, 1'b1, n7404_1_p2, 1'b0, n7486_1_p9, A[1], n7432_1_p9, A[1], n7408_1_p10, B[3], Result[0], AluOp[0], AluOp[1], n7404_1_p4, AluOp[2], 1'b0

  // Notes on the sheet:
  //   3
  //   2
  //   1
  //   0
endmodule
